// Logisim project tower.circ as structural Verilog: 12 circuits, main circuit main
module main (
);

  wire alu_1_c, alu_1_n, alu_1_v, alu_1_z, clock_1_out, undriven_7, undriven_8, undriven_13, undriven_14,
       undriven_23;
  wire [1:0] undriven_9, undriven_10, undriven_11, undriven_24, undriven_25, undriven_26;
  wire [3:0] undriven_12, undriven_15, undriven_16;
  wire [15:0] alu_1_sum, ihu_1_n1_val, ihu_1_n2_val, ihu_1_n3_val, multiplexer_1_out, multiplexer_2_out,
       multiplexer_3_out, multiplexer_4_out, ram_1_dout, regfile_1_d_b_out, undriven, undriven_2, undriven_3,
       undriven_4, undriven_5, undriven_6, undriven_17, undriven_18, undriven_19, undriven_20, undriven_21,
       undriven_22;

  Clock clock_1 (.out(clock_1_out));
  Multiplexer #(.select(2), .width(16)) multiplexer_1 (
    .in0(alu_1_sum), .in1(undriven), .in2(undriven_2), .in3(undriven_3), .out(multiplexer_1_out),
    .sel(undriven_11));
  Multiplexer #(.select(2), .width(16)) multiplexer_2 (
    .in0(regfile_1_d_b_out), .in1(undriven_4), .in2(undriven_5), .in3(undriven_6), .out(multiplexer_2_out),
    .sel(undriven_10));
  ALU alu_1 (
    .ENABLE(undriven_7), .OP_A(multiplexer_1_out), .OP_B(multiplexer_2_out), .C_IN(undriven_8),
    .OP_SEL(undriven_9), .SUM(alu_1_sum), .V(alu_1_v), .C(alu_1_c), .N(alu_1_n), .Z(alu_1_z));
  REGFILE regfile_1 (
    .D_IN(alu_1_sum), .ADDR_D(undriven_12), .CLK(undriven_13), .RESET(undriven_14), .ADDR_A(undriven_15),
    .ADDR_B(undriven_16), .D_A_OUT(alu_1_sum), .D_B_OUT(regfile_1_d_b_out));
  Multiplexer #(.select(2), .width(16)) multiplexer_3 (
    .in0(alu_1_sum), .in1(undriven_17), .in2(undriven_18), .in3(undriven_19), .out(multiplexer_3_out),
    .sel(undriven_26));
  Multiplexer #(.select(2), .width(16)) multiplexer_4 (
    .in0(regfile_1_d_b_out), .in1(undriven_20), .in2(undriven_21), .in3(undriven_22),
    .out(multiplexer_4_out), .sel(undriven_25));
  RAM #(.addrWidth(16), .dataWidth(16)) ram_1 (.clk(clock_1_out), .dout(ram_1_dout));  // open: addr, we, oe, din
  LPU lpu_1 (.ENABLE(undriven_23), .A(multiplexer_3_out), .B(multiplexer_4_out), .OPSEL(undriven_24), .O(alu_1_sum));
  IHU ihu_1 (
    .RAM_IN(ram_1_dout), .CLK(clock_1_out), .N1_VAL(ihu_1_n1_val), .N2_VAL(ihu_1_n2_val),
    .N3_VAL(ihu_1_n3_val));  // open: PC_LOAD, PC_IN, IR_IN, IR_WRITE, RESET, SC_RESET, N1_WRITE, N2_WRITE, N3_WRITE, PC_VAL, CONTROL_WORD
endmodule

module ALU (
  input  ENABLE,
  input  [15:0] OP_A,
  input  [15:0] OP_B,
  input  C_IN,
  input  [1:0] OP_SEL,
  output [15:0] SUM,
  output V,
  output C,
  output N,
  output Z
);

  wire and_1_out, and_2_out, fa_16_1_carry, fa_16_1_n, fa_16_1_v, fa_16_1_z, not_1_out, sh_16_1_carry,
       sh_16_1_n, sh_16_1_v, sh_16_1_z;
  wire [15:0] bit_extender_1_out, fa_16_1_s, multiplexer_1_out, sh_16_1_o, xor_1_out;

  not not_1 (not_1_out, OP_SEL[0]);
  and and_1 (and_1_out, ENABLE, OP_SEL[1], OP_SEL[0]);
  and and_2 (and_2_out, ENABLE, OP_SEL[1], not_1_out);
  SH_16 sh_16_1 (
    .I(OP_A), .L(C_IN), .C(and_1_out), .O(sh_16_1_o), .V(sh_16_1_v), .CARRY(sh_16_1_carry), .N(sh_16_1_n),
    .Z(sh_16_1_z));
  assign bit_extender_1_out = {{15{and_2_out}}, and_2_out};  // Bit_Extender bit_extender_1
  assign xor_1_out = OP_B ^ bit_extender_1_out;  // XOR_Gate xor_1, 16 bits wide
  Multiplexer #(.width(16)) multiplexer_1 (.in0(OP_B), .in1(xor_1_out), .out(multiplexer_1_out), .sel(and_2_out));
  FA_16 fa_16_1 (
    .A(OP_A), .B(multiplexer_1_out), .C(and_2_out), .S(fa_16_1_s), .V(fa_16_1_v), .CARRY(fa_16_1_carry),
    .N(fa_16_1_n), .Z(fa_16_1_z));
  Multiplexer #(.enable("true")) multiplexer_2 (
    .in0(fa_16_1_n), .in1(sh_16_1_n), .out(N), .sel(OP_SEL[0]), .en(ENABLE));
  Multiplexer #(.enable("true")) multiplexer_3 (
    .in0(fa_16_1_z), .in1(sh_16_1_z), .out(Z), .sel(OP_SEL[0]), .en(ENABLE));
  Multiplexer #(.enable("true")) multiplexer_4 (
    .in0(fa_16_1_v), .in1(sh_16_1_v), .out(V), .sel(OP_SEL[0]), .en(ENABLE));
  Multiplexer #(.enable("true")) multiplexer_5 (
    .in0(fa_16_1_carry), .in1(sh_16_1_carry), .out(C), .sel(OP_SEL[0]), .en(ENABLE));
  Multiplexer #(.enable("true"), .width(16)) multiplexer_6 (
    .in0(fa_16_1_s), .in1(sh_16_1_o), .out(SUM), .sel(OP_SEL[0]), .en(ENABLE));

  // Notes on the sheet:
  //   connect to bus A
  //   connect to bus B
  //   generated cin signal
  //   OPSEL codes
  //   00 / 10 / 11 / 01:
  //   add / sub / CS / LS
  //   OPB and CIN handled externally
  //   if shifting, cin used for direction
  //   CIN is high when shifting right
  //   opcode 001
  //   operation select
  //   Circular // Subtract
  //   hell world. gem world. these are the same in my slopcel eyes.
  //   subtract signal OPB inverter
endmodule

module LPU (
  input  ENABLE,
  input  [15:0] A,
  input  [15:0] B,
  input  [1:0] OPSEL,
  output [15:0] O
);

  wire [15:0] and_1_out, not_1_out, or_1_out, xor_1_out;

  assign and_1_out = B & A;  // AND_Gate and_1, 16 bits wide
  assign or_1_out = B | A;  // OR_Gate or_1, 16 bits wide
  assign not_1_out = ~A;  // NOT_Gate not_1, 16 bits wide
  Multiplexer #(.enable("true"), .select(2), .width(16)) multiplexer_1 (
    .in0(and_1_out), .in1(or_1_out), .in2(not_1_out), .in3(xor_1_out), .out(O), .sel(OPSEL), .en(ENABLE));
  assign xor_1_out = B ^ A;  // XOR_Gate xor_1, 16 bits wide
endmodule

module REGFILE (
  input  [15:0] D_IN,
  input  [3:0] ADDR_D,
  input  CLK,
  input  RESET,
  input  [3:0] ADDR_A,
  input  [3:0] ADDR_B,
  output [15:0] D_A_OUT,
  output [15:0] D_B_OUT
);

  wire decoder_1_out0, decoder_1_out1, decoder_1_out2, decoder_1_out3, decoder_2_out0, decoder_2_out1,
       decoder_2_out2, decoder_2_out3, decoder_3_out0, decoder_3_out1, decoder_3_out2, decoder_3_out3,
       decoder_4_out0, decoder_4_out1, decoder_4_out2, decoder_4_out3, decoder_5_out0, decoder_5_out1,
       decoder_5_out2, decoder_5_out3;
  wire [15:0] A_q, B_q, C_q, D_q, E_q, F_q, G_q, H_q, I_q, J_q, K_q, L_q, M_q, multiplexer_1_out,
       multiplexer_2_out, multiplexer_3_out, multiplexer_4_out, multiplexer_5_out, multiplexer_6_out,
       multiplexer_7_out, multiplexer_8_out, N_q, O_q, P_q;

  Decoder #(.enable("false"), .select(2)) decoder_1 (
    .out0(decoder_1_out0), .out1(decoder_1_out1), .out2(decoder_1_out2), .out3(decoder_1_out3),
    .sel(ADDR_D[3:2]));
  Decoder #(.select(2)) decoder_2 (
    .out0(decoder_2_out0), .out1(decoder_2_out1), .out2(decoder_2_out2), .out3(decoder_2_out3),
    .sel(ADDR_D[1:0]), .en(decoder_1_out0));
  Register #(.width(16)) D (.D(D_IN), .en(decoder_2_out3), .clk(CLK), .Q(D_q), .clr(RESET));
  Register #(.width(16)) C (.D(D_IN), .en(decoder_2_out2), .clk(CLK), .Q(C_q), .clr(RESET));
  Register #(.width(16)) B (.D(D_IN), .en(decoder_2_out1), .clk(CLK), .Q(B_q), .clr(RESET));
  Register #(.width(16)) A (.D(D_IN), .en(decoder_2_out0), .clk(CLK), .Q(A_q), .clr(RESET));
  Decoder #(.select(2)) decoder_3 (
    .out0(decoder_3_out0), .out1(decoder_3_out1), .out2(decoder_3_out2), .out3(decoder_3_out3),
    .sel(ADDR_D[1:0]), .en(decoder_1_out1));
  Multiplexer #(.select(2), .width(16)) multiplexer_1 (
    .in0(A_q), .in1(B_q), .in2(C_q), .in3(D_q), .out(multiplexer_1_out), .sel(ADDR_B[1:0]));
  Multiplexer #(.select(2), .width(16)) multiplexer_2 (
    .in0(A_q), .in1(B_q), .in2(C_q), .in3(D_q), .out(multiplexer_2_out), .sel(ADDR_A[1:0]));
  Register #(.width(16)) H (.D(D_IN), .en(decoder_3_out3), .clk(CLK), .Q(H_q), .clr(RESET));
  Register #(.width(16)) G (.D(D_IN), .en(decoder_3_out2), .clk(CLK), .Q(G_q), .clr(RESET));
  Register #(.width(16)) F (.D(D_IN), .en(decoder_3_out1), .clk(CLK), .Q(F_q), .clr(RESET));
  Register #(.width(16)) E (.D(D_IN), .en(decoder_3_out0), .clk(CLK), .Q(E_q), .clr(RESET));
  Decoder #(.select(2)) decoder_4 (
    .out0(decoder_4_out0), .out1(decoder_4_out1), .out2(decoder_4_out2), .out3(decoder_4_out3),
    .sel(ADDR_D[1:0]), .en(decoder_1_out2));
  Multiplexer #(.select(2), .width(16)) multiplexer_3 (
    .in0(E_q), .in1(F_q), .in2(G_q), .in3(H_q), .out(multiplexer_3_out), .sel(ADDR_A[1:0]));
  Register #(.width(16)) L (.D(D_IN), .en(decoder_4_out3), .clk(CLK), .Q(L_q), .clr(RESET));
  Register #(.width(16)) K (.D(D_IN), .en(decoder_4_out2), .clk(CLK), .Q(K_q), .clr(RESET));
  Register #(.width(16)) J (.D(D_IN), .en(decoder_4_out1), .clk(CLK), .Q(J_q), .clr(RESET));
  Register #(.width(16)) I (.D(D_IN), .en(decoder_4_out0), .clk(CLK), .Q(I_q), .clr(RESET));
  Multiplexer #(.select(2), .width(16)) multiplexer_4 (
    .in0(E_q), .in1(F_q), .in2(G_q), .in3(H_q), .out(multiplexer_4_out), .sel(ADDR_B[1:0]));
  Decoder #(.select(2)) decoder_5 (
    .out0(decoder_5_out0), .out1(decoder_5_out1), .out2(decoder_5_out2), .out3(decoder_5_out3),
    .sel(ADDR_D[1:0]), .en(decoder_1_out3));
  Multiplexer #(.select(2), .width(16)) multiplexer_5 (
    .in0(I_q), .in1(J_q), .in2(K_q), .in3(L_q), .out(multiplexer_5_out), .sel(ADDR_A[1:0]));
  Register #(.width(16)) P (.D(D_IN), .en(decoder_5_out3), .clk(CLK), .Q(P_q), .clr(RESET));
  Register #(.width(16)) O (.D(D_IN), .en(decoder_5_out2), .clk(CLK), .Q(O_q), .clr(RESET));
  Register #(.width(16)) N (.D(D_IN), .en(decoder_5_out1), .clk(CLK), .Q(N_q), .clr(RESET));
  Register #(.width(16)) M (.D(D_IN), .en(decoder_5_out0), .clk(CLK), .Q(M_q), .clr(RESET));
  Multiplexer #(.select(2), .width(16)) multiplexer_6 (
    .in0(I_q), .in1(J_q), .in2(K_q), .in3(L_q), .out(multiplexer_6_out), .sel(ADDR_B[1:0]));
  Multiplexer #(.select(2), .width(16)) multiplexer_7 (
    .in0(M_q), .in1(N_q), .in2(O_q), .in3(P_q), .out(multiplexer_7_out), .sel(ADDR_A[1:0]));
  Multiplexer #(.select(2), .width(16)) multiplexer_8 (
    .in0(M_q), .in1(N_q), .in2(O_q), .in3(P_q), .out(multiplexer_8_out), .sel(ADDR_B[1:0]));
  Multiplexer #(.select(2), .width(16)) multiplexer_9 (
    .in0(multiplexer_2_out), .in1(multiplexer_3_out), .in2(multiplexer_5_out), .in3(multiplexer_7_out),
    .out(D_A_OUT), .sel(ADDR_A[3:2]));
  Multiplexer #(.select(2), .width(16)) multiplexer_10 (
    .in0(multiplexer_1_out), .in1(multiplexer_4_out), .in2(multiplexer_6_out), .in3(multiplexer_8_out),
    .out(D_B_OUT), .sel(ADDR_B[3:2]));

  // Notes on the sheet:
  //   ROW
  //   COL
  //   addr_d acts as a write trigger
endmodule

module IHU (
  input  PC_LOAD,
  input  [15:0] PC_IN,
  input  [15:0] RAM_IN,
  input  [15:0] IR_IN,
  input  IR_WRITE,
  input  CLK,
  input  RESET,
  input  SC_RESET,
  input  N1_WRITE,
  input  N2_WRITE,
  input  N3_WRITE,
  output [15:0] PC_VAL,
  output [31:0] CONTROL_WORD,
  output [15:0] N1_VAL,
  output [15:0] N2_VAL,
  output [15:0] N3_VAL
);

  wire or_1_out, SC_carry;
  wire [3:0] SC_q, undriven;
  wire [15:0] IR_q;

  FA_16 fa_16_1 ();  // open: A, B, C, S, V, CARRY, N, Z
  // NoConnect on undriven
  Register #(.width(16)) IR (.D(IR_IN), .en(IR_WRITE), .clk(CLK), .Q(IR_q), .clr(RESET));
  Register #(.width(16)) n_plus_1 (.D(RAM_IN), .en(N1_WRITE), .clk(CLK), .Q(N1_VAL), .clr(RESET));
  Register #(.width(16)) n_plus_2 (.D(RAM_IN), .en(N2_WRITE), .clk(CLK), .Q(N2_VAL), .clr(RESET));
  Register #(.width(16)) n_plus_3 (.D(RAM_IN), .en(N3_WRITE), .clk(CLK), .Q(N3_VAL), .clr(RESET));
  Counter #(.max('hffff), .width(16)) PC (
    .load(PC_LOAD), .D(PC_IN), .count(SC_carry), .Q(PC_VAL), .clk(CLK), .clr(RESET));  // open: carry, up
  Counter #(.max('hf), .width(4)) SC (
    .D(undriven), .count(CLK), .Q(SC_q), .carry(SC_carry), .clk(CLK), .clr(or_1_out));  // open: load, up
  or or_1 (or_1_out, SC_RESET, RESET);
  ROM #(.addrWidth(13), .dataWidth(32)) fuuuuuck (.addr({SC_q, IR_q[8:0]}), .data(CONTROL_WORD));

  // Notes on the sheet:
  //   (instruction handling unit)
  //   pc // ir  // sc // control rom
endmodule

module FA_16 (
  input  [15:0] A,
  input  [15:0] B,
  input  C,
  output [15:0] S,
  output V,
  output CARRY,
  output N,
  output Z
);

  wire fa_4_1_o, fa_4_2_o, fa_4_3_o;

  FA_4 fa_4_1 (.A(A[3:0]), .B(B[3:0]), .C(C), .S(S[3:0]), .O(fa_4_1_o));
  FA_4 fa_4_2 (.A(A[7:4]), .B(B[7:4]), .C(fa_4_1_o), .S(S[7:4]), .O(fa_4_2_o));
  FA_4 fa_4_3 (.A(A[11:8]), .B(B[11:8]), .C(fa_4_2_o), .S(S[11:8]), .O(fa_4_3_o));
  FA_4 fa_4_4 (.A(A[15:12]), .B(B[15:12]), .C(fa_4_3_o), .S({N, S[14:12]}), .O(CARRY));
  xor xor_1 (V, CARRY, C);
  or or_1 (Z, N, S[14], S[13], S[12], S[11], S[10], S[9], S[8], S[7], S[6], S[5], S[4], S[3], S[2], S[1], S[0]);

  assign S[15] = N;
endmodule

module FA_4 (
  input  [3:0] A,
  input  [3:0] B,
  input  C,
  output [3:0] S,
  output O
);

  wire fa_1_1_o, fa_1_2_o, fa_1_3_o;

  FA_1 fa_1_1 (.A(A[0]), .B(B[0]), .C(C), .S(S[0]), .O(fa_1_1_o));
  FA_1 fa_1_2 (.A(A[1]), .B(B[1]), .C(fa_1_1_o), .S(S[1]), .O(fa_1_2_o));
  FA_1 fa_1_3 (.A(A[2]), .B(B[2]), .C(fa_1_2_o), .S(S[2]), .O(fa_1_3_o));
  FA_1 fa_1_4 (.A(A[3]), .B(B[3]), .C(fa_1_3_o), .S(S[3]), .O(O));
endmodule

module FA_1 (
  input  A,
  input  B,
  input  C,
  output S,
  output O
);

  wire and_1_out, and_2_out, xor_1_out;

  xor xor_1 (xor_1_out, A, B);
  and and_1 (and_1_out, A, B);
  xor xor_2 (S, xor_1_out, C);
  and and_2 (and_2_out, xor_1_out, C);
  or or_1 (O, and_1_out, and_2_out);
endmodule

module SH_16 (
  input  [15:0] I,
  input  L,
  input  C,
  output [15:0] O,
  output V,
  output CARRY,
  output N,
  output Z
);

  wire or_1_out;

  Multiplexer #(.select(2), .width(16)) multiplexer_1 (
    .in0({1'b0, I[15:1]}), .in1({I[0], I[15:1]}), .in2({I[14:0], 1'b0}), .in3({I[14:0], I[15]}),
    .out({N, O[14:0]}), .sel({L, C}));
  or or_1 (or_1_out, N, O[14], O[13], O[12], O[11], O[10], O[9], O[8], O[7], O[6], O[5], O[4], O[3], O[2], O[1], O[0]);
  not not_1 (Z, or_1_out);
  Multiplexer #(.select(2)) multiplexer_2 (.in0(I[0]), .in1(1'b0), .in2(I[15]), .in3(1'b0), .out(V), .sel({L, C}));

  assign CARRY = 1'b0;
  assign O[15] = N;

  // Notes on the sheet:
  //   Left shift?
  //   Circular shift?
endmodule

module BL_16 (
  input  [15:0] A,
  input  [15:0] B,
  input  [1:0] I,
  output [15:0] O
);

  wire [15:0] and_1_out, not_1_out, or_1_out, xor_1_out;

  assign and_1_out = B & A;  // AND_Gate and_1, 16 bits wide
  assign or_1_out = B | A;  // OR_Gate or_1, 16 bits wide
  assign not_1_out = ~A;  // NOT_Gate not_1, 16 bits wide
  assign xor_1_out = B ^ A;  // XOR_Gate xor_1, 16 bits wide
  Multiplexer #(.select(2), .width(16)) multiplexer_1 (
    .in0(and_1_out), .in1(or_1_out), .in2(not_1_out), .in3(xor_1_out), .out(O), .sel(I));
endmodule

module FA_16_TTL (
  input  A1,
  input  A2,
  input  in_3,
  input  in_4,
  input  in_5,
  input  in_6,
  input  in_7,
  input  in_8,
  input  in_9,
  input  in_10,
  input  in_11,
  input  in_12,
  input  in_13,
  input  in_14,
  input  in_15,
  input  in_16,
  input  B1,
  input  B2,
  input  in_19,
  input  in_20,
  input  C,
  output S,
  output out_23
);

  wire transistor_1_out, transistor_4_out, transistor_5_out, transistor_8_out, transistor_9_out,
       transistor_12_out, transistor_13_out, transistor_16_out, transistor_17_out, transistor_18_out,
       transistor_21_out, transistor_23_out, transistor_24_out, transistor_27_out, transistor_29_out,
       transistor_30_out, transistor_32_out, transistor_34_out, transistor_35_out, transistor_37_out,
       transistor_40_out, transistor_43_out, transistor_45_out, transistor_48_out, transistor_49_out,
       transistor_52_out, transistor_53_out, transistor_56_out, transistor_57_out, transistor_60_out,
       transistor_61_out, transistor_62_out, transistor_63_out, transistor_67_out, transistor_68_out,
       transistor_69_out, transistor_72_out, transistor_73_out, transistor_74_out, transistor_78_out,
       transistor_79_out, transistor_80_out, transistor_83_out, transistor_85_out, transistor_86_out,
       transistor_89_out, transistor_91_out, transistor_92_out, transistor_101_out, transistor_104_out,
       transistor_105_out, transistor_107_out, transistor_109_out, transistor_111_out, transistor_114_out,
       transistor_115_out, transistor_117_out, transistor_119_out, transistor_121_out, transistor_122_out,
       transistor_123_out, transistor_127_out, transistor_128_out, transistor_129_out, transistor_133_out,
       transistor_135_out, transistor_136_out, transistor_138_out, transistor_140_out, transistor_143_out,
       transistor_145_out, transistor_148_out, transistor_149_out, transistor_151_out, transistor_153_out,
       transistor_155_out, transistor_158_out, transistor_159_out, transistor_161_out, transistor_163_out,
       transistor_165_out, transistor_166_out, transistor_167_out, transistor_171_out, transistor_172_out,
       transistor_174_out, transistor_175_out, transistor_176_out, transistor_180_out, transistor_181_out,
       transistor_183_out, transistor_186_out, transistor_187_out, transistor_190_out, transistor_193_out,
       transistor_194_out, transistor_197_out, transistor_199_out;

  Transistor transistor_1 (.in(1'b1), .out(transistor_1_out), .gate(A1));
  Transistor transistor_2 (.in(1'b1), .out(transistor_1_out), .gate(B1));
  Transistor #(.\type ("n")) transistor_3 (.in(transistor_4_out), .out(transistor_1_out), .gate(A1));
  Transistor #(.\type ("n")) transistor_4 (.in(1'b0), .out(transistor_4_out), .gate(B1));
  Transistor transistor_5 (.in(1'b1), .out(transistor_5_out), .gate(A1));
  Transistor transistor_6 (.in(1'b1), .out(transistor_5_out), .gate(B1));
  Transistor #(.\type ("n")) transistor_7 (.in(transistor_8_out), .out(transistor_5_out), .gate(A1));
  Transistor #(.\type ("n")) transistor_8 (.in(1'b0), .out(transistor_8_out), .gate(B1));
  Transistor transistor_9 (.in(1'b1), .out(transistor_9_out), .gate(A2));
  Transistor transistor_10 (.in(1'b1), .out(transistor_9_out), .gate(B2));
  Transistor #(.\type ("n")) transistor_11 (.in(transistor_12_out), .out(transistor_9_out), .gate(A2));
  Transistor #(.\type ("n")) transistor_12 (.in(1'b0), .out(transistor_12_out), .gate(B2));
  Transistor transistor_13 (.in(1'b1), .out(transistor_13_out), .gate(A2));
  Transistor transistor_14 (.in(1'b1), .out(transistor_13_out), .gate(B2));
  Transistor #(.\type ("n")) transistor_15 (.in(transistor_16_out), .out(transistor_13_out), .gate(A2));
  Transistor #(.\type ("n")) transistor_16 (.in(1'b0), .out(transistor_16_out), .gate(B2));
  Transistor transistor_17 (.in(1'b1), .out(transistor_17_out), .gate(A1));
  Transistor transistor_18 (.in(transistor_17_out), .out(transistor_18_out), .gate(B1));
  Transistor #(.\type ("n")) transistor_19 (.in(1'b0), .out(transistor_18_out), .gate(B1));
  Transistor #(.\type ("n")) transistor_20 (.in(1'b0), .out(transistor_18_out), .gate(A1));
  Transistor transistor_21 (.in(1'b1), .out(transistor_21_out), .gate(transistor_5_out));
  Transistor #(.\type ("n")) transistor_22 (.in(1'b0), .out(transistor_21_out), .gate(transistor_5_out));
  Transistor transistor_23 (.in(1'b1), .out(transistor_23_out), .gate(A2));
  Transistor transistor_24 (.in(transistor_23_out), .out(transistor_24_out), .gate(B2));
  Transistor #(.\type ("n")) transistor_25 (.in(1'b0), .out(transistor_24_out), .gate(B2));
  Transistor #(.\type ("n")) transistor_26 (.in(1'b0), .out(transistor_24_out), .gate(A2));
  Transistor transistor_27 (.in(1'b1), .out(transistor_27_out), .gate(transistor_13_out));
  Transistor #(.\type ("n")) transistor_28 (.in(1'b0), .out(transistor_27_out), .gate(transistor_13_out));
  Transistor transistor_29 (.in(1'b1), .out(transistor_29_out), .gate(transistor_18_out));
  Transistor transistor_30 (.in(1'b1), .out(transistor_30_out), .gate(transistor_29_out));
  Transistor #(.\type ("n")) transistor_31 (.in(transistor_32_out), .out(transistor_30_out), .gate(transistor_29_out));
  Transistor #(.\type ("n")) transistor_32 (.in(1'b0), .out(transistor_32_out), .gate(transistor_1_out));
  Transistor #(.\type ("n")) transistor_33 (.in(1'b0), .out(transistor_29_out), .gate(transistor_18_out));
  Transistor transistor_34 (.in(1'b1), .out(transistor_34_out), .gate(transistor_24_out));
  Transistor transistor_35 (.in(1'b1), .out(transistor_35_out), .gate(transistor_34_out));
  Transistor #(.\type ("n")) transistor_36 (.in(transistor_37_out), .out(transistor_35_out), .gate(transistor_34_out));
  Transistor #(.\type ("n")) transistor_37 (.in(1'b0), .out(transistor_37_out), .gate(transistor_9_out));
  Transistor #(.\type ("n")) transistor_38 (.in(1'b0), .out(transistor_34_out), .gate(transistor_24_out));
  Transistor transistor_39 (.in(1'b1), .out(transistor_30_out), .gate(transistor_1_out));
  Transistor transistor_40 (.in(1'b1), .out(transistor_40_out), .gate(transistor_30_out));
  Transistor #(.\type ("n")) transistor_41 (.in(1'b0), .out(transistor_40_out), .gate(transistor_30_out));
  Transistor transistor_42 (.in(1'b1), .out(transistor_35_out), .gate(transistor_9_out));
  Transistor transistor_43 (.in(1'b1), .out(transistor_43_out), .gate(transistor_35_out));
  Transistor #(.\type ("n")) transistor_44 (.in(1'b0), .out(transistor_43_out), .gate(transistor_35_out));
  Transistor transistor_45 (.in(1'b1), .out(transistor_45_out), .gate(C));
  Transistor transistor_46 (.in(1'b1), .out(transistor_45_out), .gate(transistor_40_out));
  Transistor #(.\type ("n")) transistor_47 (.in(transistor_48_out), .out(transistor_45_out), .gate(C));
  Transistor #(.\type ("n")) transistor_48 (.in(1'b0), .out(transistor_48_out), .gate(transistor_40_out));
  Transistor transistor_49 (.in(1'b1), .out(transistor_49_out), .gate(transistor_40_out));
  Transistor transistor_50 (.in(1'b1), .out(transistor_49_out), .gate(C));
  Transistor #(.\type ("n")) transistor_51 (.in(transistor_52_out), .out(transistor_49_out), .gate(transistor_40_out));
  Transistor #(.\type ("n")) transistor_52 (.in(1'b0), .out(transistor_52_out), .gate(C));
  Transistor transistor_53 (.in(1'b1), .out(transistor_53_out), .gate(transistor_86_out));
  Transistor transistor_54 (.in(1'b1), .out(transistor_53_out), .gate(transistor_43_out));
  Transistor #(.\type ("n")) transistor_55 (.in(transistor_56_out), .out(transistor_53_out), .gate(transistor_86_out));
  Transistor #(.\type ("n")) transistor_56 (.in(1'b0), .out(transistor_56_out), .gate(transistor_43_out));
  Transistor transistor_57 (.in(1'b1), .out(transistor_57_out), .gate(transistor_43_out));
  Transistor transistor_58 (.in(1'b1), .out(transistor_57_out), .gate(transistor_86_out));
  Transistor #(.\type ("n")) transistor_59 (.in(transistor_60_out), .out(transistor_57_out), .gate(transistor_43_out));
  Transistor #(.\type ("n")) transistor_60 (.in(1'b0), .out(transistor_60_out), .gate(transistor_86_out));
  Transistor transistor_61 (.in(1'b1), .out(transistor_61_out), .gate(C));
  Transistor transistor_62 (.in(1'b1), .out(transistor_62_out), .gate(transistor_63_out));
  Transistor transistor_63 (.in(transistor_61_out), .out(transistor_63_out), .gate(transistor_40_out));
  Transistor #(.\type ("n")) transistor_64 (.in(1'b0), .out(transistor_63_out), .gate(transistor_40_out));
  Transistor #(.\type ("n")) transistor_65 (.in(1'b0), .out(transistor_63_out), .gate(C));
  Transistor #(.\type ("n")) transistor_66 (.in(1'b0), .out(transistor_62_out), .gate(transistor_63_out));
  Transistor transistor_67 (.in(1'b1), .out(transistor_67_out), .gate(transistor_49_out));
  Transistor transistor_68 (.in(1'b1), .out(transistor_68_out), .gate(transistor_21_out));
  Transistor transistor_69 (.in(transistor_68_out), .out(transistor_69_out), .gate(transistor_67_out));
  Transistor #(.\type ("n")) transistor_70 (.in(1'b0), .out(transistor_69_out), .gate(transistor_67_out));
  Transistor #(.\type ("n")) transistor_71 (.in(1'b0), .out(transistor_67_out), .gate(transistor_49_out));
  Transistor transistor_72 (.in(1'b1), .out(transistor_72_out), .gate(transistor_86_out));
  Transistor transistor_73 (.in(1'b1), .out(transistor_73_out), .gate(transistor_74_out));
  Transistor transistor_74 (.in(transistor_72_out), .out(transistor_74_out), .gate(transistor_43_out));
  Transistor #(.\type ("n")) transistor_75 (.in(1'b0), .out(transistor_74_out), .gate(transistor_43_out));
  Transistor #(.\type ("n")) transistor_76 (.in(1'b0), .out(transistor_74_out), .gate(transistor_86_out));
  Transistor #(.\type ("n")) transistor_77 (.in(1'b0), .out(transistor_73_out), .gate(transistor_74_out));
  Transistor transistor_78 (.in(1'b1), .out(transistor_78_out), .gate(transistor_57_out));
  Transistor transistor_79 (.in(1'b1), .out(transistor_79_out), .gate(transistor_27_out));
  Transistor transistor_80 (.in(transistor_79_out), .out(transistor_80_out), .gate(transistor_78_out));
  Transistor #(.\type ("n")) transistor_81 (.in(1'b0), .out(transistor_80_out), .gate(transistor_78_out));
  Transistor #(.\type ("n")) transistor_82 (.in(1'b0), .out(transistor_78_out), .gate(transistor_57_out));
  Transistor transistor_83 (.in(1'b1), .out(transistor_83_out), .gate(transistor_62_out));
  Transistor #(.\type ("n")) transistor_84 (.in(transistor_85_out), .out(transistor_83_out), .gate(transistor_62_out));
  Transistor #(.\type ("n")) transistor_85 (.in(1'b0), .out(transistor_85_out), .gate(transistor_45_out));
  Transistor transistor_86 (.in(1'b1), .out(transistor_86_out), .gate(transistor_69_out));
  Transistor #(.\type ("n")) transistor_87 (.in(1'b0), .out(transistor_69_out), .gate(transistor_21_out));
  Transistor #(.\type ("n")) transistor_88 (.in(1'b0), .out(transistor_86_out), .gate(transistor_69_out));
  Transistor transistor_89 (.in(1'b1), .out(transistor_89_out), .gate(transistor_73_out));
  Transistor #(.\type ("n")) transistor_90 (.in(transistor_91_out), .out(transistor_89_out), .gate(transistor_73_out));
  Transistor #(.\type ("n")) transistor_91 (.in(1'b0), .out(transistor_91_out), .gate(transistor_53_out));
  Transistor transistor_92 (.in(1'b1), .out(transistor_92_out), .gate(transistor_80_out));
  Transistor #(.\type ("n")) transistor_93 (.in(1'b0), .out(transistor_80_out), .gate(transistor_27_out));
  Transistor #(.\type ("n")) transistor_94 (.in(1'b0), .out(transistor_92_out), .gate(transistor_80_out));
  Transistor transistor_95 (.in(1'b1), .out(transistor_83_out), .gate(transistor_45_out));
  Transistor transistor_96 (.in(1'b1), .out(S), .gate(transistor_83_out));
  Transistor #(.\type ("n")) transistor_97 (.in(1'b0), .out(S), .gate(transistor_83_out));
  Transistor transistor_98 (.in(1'b1), .out(transistor_89_out), .gate(transistor_53_out));
  Transistor transistor_99 (.in(1'b1), .out(out_23), .gate(transistor_89_out));
  Transistor #(.\type ("n")) transistor_100 (.in(1'b0), .out(out_23), .gate(transistor_89_out));
  Transistor transistor_101 (.in(1'b1), .out(transistor_101_out), .gate(in_3));
  Transistor transistor_102 (.in(1'b1), .out(transistor_101_out), .gate(in_19));
  Transistor #(.\type ("n")) transistor_103 (.in(transistor_104_out), .out(transistor_101_out), .gate(in_3));
  Transistor #(.\type ("n")) transistor_104 (.in(1'b0), .out(transistor_104_out), .gate(in_19));
  Transistor transistor_105 (.in(1'b1), .out(transistor_105_out), .gate(in_3));
  Transistor transistor_106 (.in(1'b1), .out(transistor_105_out), .gate(in_19));
  Transistor transistor_107 (.in(1'b1), .out(transistor_107_out), .gate(transistor_105_out));
  Transistor #(.\type ("n")) transistor_108 (.in(transistor_109_out), .out(transistor_105_out), .gate(in_3));
  Transistor #(.\type ("n")) transistor_109 (.in(1'b0), .out(transistor_109_out), .gate(in_19));
  Transistor #(.\type ("n")) transistor_110 (.in(1'b0), .out(transistor_107_out), .gate(transistor_105_out));
  Transistor transistor_111 (.in(1'b1), .out(transistor_111_out), .gate(in_4));
  Transistor transistor_112 (.in(1'b1), .out(transistor_111_out), .gate(in_20));
  Transistor #(.\type ("n")) transistor_113 (.in(transistor_114_out), .out(transistor_111_out), .gate(in_4));
  Transistor #(.\type ("n")) transistor_114 (.in(1'b0), .out(transistor_114_out), .gate(in_20));
  Transistor transistor_115 (.in(1'b1), .out(transistor_115_out), .gate(in_4));
  Transistor transistor_116 (.in(1'b1), .out(transistor_115_out), .gate(in_20));
  Transistor transistor_117 (.in(1'b1), .out(transistor_117_out), .gate(transistor_115_out));
  Transistor #(.\type ("n")) transistor_118 (.in(transistor_119_out), .out(transistor_115_out), .gate(in_4));
  Transistor #(.\type ("n")) transistor_119 (.in(1'b0), .out(transistor_119_out), .gate(in_20));
  Transistor #(.\type ("n")) transistor_120 (.in(1'b0), .out(transistor_117_out), .gate(transistor_115_out));
  Transistor transistor_121 (.in(1'b1), .out(transistor_121_out), .gate(in_3));
  Transistor transistor_122 (.in(1'b1), .out(transistor_122_out), .gate(transistor_123_out));
  Transistor transistor_123 (.in(transistor_121_out), .out(transistor_123_out), .gate(in_19));
  Transistor #(.\type ("n")) transistor_124 (.in(1'b0), .out(transistor_123_out), .gate(in_19));
  Transistor #(.\type ("n")) transistor_125 (.in(1'b0), .out(transistor_123_out), .gate(in_3));
  Transistor #(.\type ("n")) transistor_126 (.in(1'b0), .out(transistor_122_out), .gate(transistor_123_out));
  Transistor transistor_127 (.in(1'b1), .out(transistor_127_out), .gate(in_4));
  Transistor transistor_128 (.in(1'b1), .out(transistor_128_out), .gate(transistor_129_out));
  Transistor transistor_129 (.in(transistor_127_out), .out(transistor_129_out), .gate(in_20));
  Transistor #(.\type ("n")) transistor_130 (.in(1'b0), .out(transistor_129_out), .gate(in_20));
  Transistor #(.\type ("n")) transistor_131 (.in(1'b0), .out(transistor_129_out), .gate(in_4));
  Transistor #(.\type ("n")) transistor_132 (.in(1'b0), .out(transistor_128_out), .gate(transistor_129_out));
  Transistor transistor_133 (.in(1'b1), .out(transistor_133_out), .gate(transistor_122_out));
  Transistor #(.\type ("n")) transistor_134 (
    .in(transistor_135_out), .out(transistor_133_out), .gate(transistor_122_out));
  Transistor #(.\type ("n")) transistor_135 (.in(1'b0), .out(transistor_135_out), .gate(transistor_101_out));
  Transistor transistor_136 (.in(1'b1), .out(transistor_136_out), .gate(transistor_128_out));
  Transistor #(.\type ("n")) transistor_137 (
    .in(transistor_138_out), .out(transistor_136_out), .gate(transistor_128_out));
  Transistor #(.\type ("n")) transistor_138 (.in(1'b0), .out(transistor_138_out), .gate(transistor_111_out));
  Transistor transistor_139 (.in(1'b1), .out(transistor_133_out), .gate(transistor_101_out));
  Transistor transistor_140 (.in(1'b1), .out(transistor_140_out), .gate(transistor_133_out));
  Transistor #(.\type ("n")) transistor_141 (.in(1'b0), .out(transistor_140_out), .gate(transistor_133_out));
  Transistor transistor_142 (.in(1'b1), .out(transistor_136_out), .gate(transistor_111_out));
  Transistor transistor_143 (.in(1'b1), .out(transistor_143_out), .gate(transistor_136_out));
  Transistor #(.\type ("n")) transistor_144 (.in(1'b0), .out(transistor_143_out), .gate(transistor_136_out));
  Transistor transistor_145 (.in(1'b1), .out(transistor_145_out), .gate(transistor_92_out));
  Transistor transistor_146 (.in(1'b1), .out(transistor_145_out), .gate(transistor_140_out));
  Transistor #(.\type ("n")) transistor_147 (
    .in(transistor_148_out), .out(transistor_145_out), .gate(transistor_92_out));
  Transistor #(.\type ("n")) transistor_148 (.in(1'b0), .out(transistor_148_out), .gate(transistor_140_out));
  Transistor transistor_149 (.in(1'b1), .out(transistor_149_out), .gate(transistor_140_out));
  Transistor transistor_150 (.in(1'b1), .out(transistor_149_out), .gate(transistor_92_out));
  Transistor transistor_151 (.in(1'b1), .out(transistor_151_out), .gate(transistor_149_out));
  Transistor #(.\type ("n")) transistor_152 (
    .in(transistor_153_out), .out(transistor_149_out), .gate(transistor_140_out));
  Transistor #(.\type ("n")) transistor_153 (.in(1'b0), .out(transistor_153_out), .gate(transistor_92_out));
  Transistor #(.\type ("n")) transistor_154 (.in(1'b0), .out(transistor_151_out), .gate(transistor_149_out));
  Transistor transistor_155 (.in(1'b1), .out(transistor_155_out), .gate(transistor_187_out));
  Transistor transistor_156 (.in(1'b1), .out(transistor_155_out), .gate(transistor_143_out));
  Transistor #(.\type ("n")) transistor_157 (
    .in(transistor_158_out), .out(transistor_155_out), .gate(transistor_187_out));
  Transistor #(.\type ("n")) transistor_158 (.in(1'b0), .out(transistor_158_out), .gate(transistor_143_out));
  Transistor transistor_159 (.in(1'b1), .out(transistor_159_out), .gate(transistor_143_out));
  Transistor transistor_160 (.in(1'b1), .out(transistor_159_out), .gate(transistor_187_out));
  Transistor transistor_161 (.in(1'b1), .out(transistor_161_out), .gate(transistor_159_out));
  Transistor #(.\type ("n")) transistor_162 (
    .in(transistor_163_out), .out(transistor_159_out), .gate(transistor_143_out));
  Transistor #(.\type ("n")) transistor_163 (.in(1'b0), .out(transistor_163_out), .gate(transistor_187_out));
  Transistor #(.\type ("n")) transistor_164 (.in(1'b0), .out(transistor_161_out), .gate(transistor_159_out));
  Transistor transistor_165 (.in(1'b1), .out(transistor_165_out), .gate(transistor_92_out));
  Transistor transistor_166 (.in(1'b1), .out(transistor_166_out), .gate(transistor_167_out));
  Transistor transistor_167 (.in(transistor_165_out), .out(transistor_167_out), .gate(transistor_140_out));
  Transistor #(.\type ("n")) transistor_168 (.in(1'b0), .out(transistor_167_out), .gate(transistor_140_out));
  Transistor #(.\type ("n")) transistor_169 (.in(1'b0), .out(transistor_167_out), .gate(transistor_92_out));
  Transistor #(.\type ("n")) transistor_170 (.in(1'b0), .out(transistor_166_out), .gate(transistor_167_out));
  Transistor transistor_171 (.in(1'b1), .out(transistor_171_out), .gate(transistor_107_out));
  Transistor transistor_172 (.in(transistor_171_out), .out(transistor_172_out), .gate(transistor_151_out));
  Transistor #(.\type ("n")) transistor_173 (.in(1'b0), .out(transistor_172_out), .gate(transistor_151_out));
  Transistor transistor_174 (.in(1'b1), .out(transistor_174_out), .gate(transistor_187_out));
  Transistor transistor_175 (.in(1'b1), .out(transistor_175_out), .gate(transistor_176_out));
  Transistor transistor_176 (.in(transistor_174_out), .out(transistor_176_out), .gate(transistor_143_out));
  Transistor #(.\type ("n")) transistor_177 (.in(1'b0), .out(transistor_176_out), .gate(transistor_143_out));
  Transistor #(.\type ("n")) transistor_178 (.in(1'b0), .out(transistor_176_out), .gate(transistor_187_out));
  Transistor #(.\type ("n")) transistor_179 (.in(1'b0), .out(transistor_175_out), .gate(transistor_176_out));
  Transistor transistor_180 (.in(1'b1), .out(transistor_180_out), .gate(transistor_117_out));
  Transistor transistor_181 (.in(transistor_180_out), .out(transistor_181_out), .gate(transistor_161_out));
  Transistor #(.\type ("n")) transistor_182 (.in(1'b0), .out(transistor_181_out), .gate(transistor_161_out));
  Transistor transistor_183 (.in(1'b1), .out(transistor_183_out), .gate(transistor_166_out));
  Transistor transistor_184 (.in(1'b1), .out(transistor_183_out), .gate(transistor_145_out));
  Transistor #(.\type ("n")) transistor_185 (
    .in(transistor_186_out), .out(transistor_183_out), .gate(transistor_166_out));
  Transistor #(.\type ("n")) transistor_186 (.in(1'b0), .out(transistor_186_out), .gate(transistor_145_out));
  Transistor transistor_187 (.in(1'b1), .out(transistor_187_out), .gate(transistor_172_out));
  Transistor #(.\type ("n")) transistor_188 (.in(1'b0), .out(transistor_172_out), .gate(transistor_107_out));
  Transistor #(.\type ("n")) transistor_189 (.in(1'b0), .out(transistor_187_out), .gate(transistor_172_out));
  Transistor transistor_190 (.in(1'b1), .out(transistor_190_out), .gate(transistor_175_out));
  Transistor transistor_191 (.in(1'b1), .out(transistor_190_out), .gate(transistor_155_out));
  Transistor #(.\type ("n")) transistor_192 (
    .in(transistor_193_out), .out(transistor_190_out), .gate(transistor_175_out));
  Transistor #(.\type ("n")) transistor_193 (.in(1'b0), .out(transistor_193_out), .gate(transistor_155_out));
  Transistor transistor_194 (.in(1'b1), .out(transistor_194_out), .gate(transistor_181_out));
  Transistor #(.\type ("n")) transistor_195 (.in(1'b0), .out(transistor_181_out), .gate(transistor_117_out));
  Transistor #(.\type ("n")) transistor_196 (.in(1'b0), .out(transistor_194_out), .gate(transistor_181_out));
  Transistor transistor_197 (.in(1'b1), .out(transistor_197_out), .gate(transistor_183_out));
  Transistor #(.\type ("n")) transistor_198 (.in(1'b0), .out(transistor_197_out), .gate(transistor_183_out));
  Transistor transistor_199 (.in(1'b1), .out(transistor_199_out), .gate(transistor_190_out));
  Transistor #(.\type ("n")) transistor_200 (.in(1'b0), .out(transistor_199_out), .gate(transistor_190_out));
endmodule

module TTL_SUBS (
  input  in_1,
  input  in_2,
  input  in_3,
  input  in_4,
  input  in_5,
  input  in_6,
  input  in_7
);

  wire transistor_1_out, transistor_3_out, transistor_6_out, transistor_7_out, transistor_8_out,
       transistor_11_out, transistor_14_out, transistor_15_out, transistor_16_out, transistor_17_out,
       transistor_21_out, transistor_23_out, transistor_25_out;

  Transistor transistor_1 (.in(1'b1), .out(transistor_1_out), .gate(in_4));
  Transistor #(.\type ("n")) transistor_2 (.in(1'b0), .out(transistor_1_out), .gate(in_4));
  // NOT_Gate not_1 is placed but not wired
  // NAND_Gate nand_1 is placed but not wired
  Transistor transistor_3 (.in(1'b1), .out(transistor_3_out), .gate(in_1));
  Transistor transistor_4 (.in(1'b1), .out(transistor_3_out), .gate(in_5));
  Transistor #(.\type ("n")) transistor_5 (.in(transistor_6_out), .out(transistor_3_out), .gate(in_1));
  Transistor #(.\type ("n")) transistor_6 (.in(1'b0), .out(transistor_6_out), .gate(in_5));
  Transistor transistor_7 (.in(1'b1), .out(transistor_7_out), .gate(in_2));
  Transistor transistor_8 (.in(transistor_7_out), .out(transistor_8_out), .gate(in_6));
  Transistor #(.\type ("n")) transistor_9 (.in(1'b0), .out(transistor_8_out), .gate(in_6));
  // NOR_Gate nor_1 is placed but not wired
  Transistor #(.\type ("n")) transistor_10 (.in(1'b0), .out(transistor_8_out), .gate(in_2));
  Transistor transistor_11 (.in(1'b1), .out(transistor_11_out), .gate(in_7));
  Transistor transistor_12 (.in(1'b1), .out(transistor_11_out), .gate(in_3));
  Transistor #(.\type ("n")) transistor_13 (.in(transistor_14_out), .out(transistor_11_out), .gate(in_3));
  Transistor #(.\type ("n")) transistor_14 (.in(1'b0), .out(transistor_14_out), .gate(in_7));
  // XOR_Gate xor_1 is placed but not wired
  Transistor transistor_15 (.in(1'b1), .out(transistor_15_out), .gate(in_3));
  Transistor transistor_16 (.in(1'b1), .out(transistor_16_out), .gate(transistor_17_out));
  Transistor transistor_17 (.in(transistor_15_out), .out(transistor_17_out), .gate(in_7));
  Transistor #(.\type ("n")) transistor_18 (.in(1'b0), .out(transistor_17_out), .gate(in_7));
  Transistor #(.\type ("n")) transistor_19 (.in(1'b0), .out(transistor_17_out), .gate(in_3));
  Transistor #(.\type ("n")) transistor_20 (.in(1'b0), .out(transistor_16_out), .gate(transistor_17_out));
  Transistor transistor_21 (.in(1'b1), .out(transistor_21_out), .gate(transistor_16_out));
  Transistor #(.\type ("n")) transistor_22 (.in(transistor_23_out), .out(transistor_21_out), .gate(transistor_16_out));
  Transistor #(.\type ("n")) transistor_23 (.in(1'b0), .out(transistor_23_out), .gate(transistor_11_out));
  Transistor transistor_24 (.in(1'b1), .out(transistor_21_out), .gate(transistor_11_out));
  Transistor transistor_25 (.in(1'b1), .out(transistor_25_out), .gate(transistor_21_out));
  Transistor #(.\type ("n")) transistor_26 (.in(1'b0), .out(transistor_25_out), .gate(transistor_21_out));
endmodule
